// Logisim project 2to4DEC.circ as structural Verilog
module DEC2to4 (
  input  [1:0] in_1,
  output [3:0] out_2
);

  nand nand_1 (out_2[0], ~in_1[0], ~in_1[1]);  // NAND_Gate
  nand nand_2 (out_2[1], in_1[0], ~in_1[1]);  // NAND_Gate
  nand nand_3 (out_2[2], ~in_1[0], in_1[1]);  // NAND_Gate
  nand nand_4 (out_2[3], in_1[0], in_1[1]);
endmodule
